# Fritzing sketch Gameboy Teleton (saved by Fritzing 0.9.3b)

parts:
  Mod1 = Raspberry Pi Pico
  S1 = Pushbutton [package="[SMD]"]
  S2 = Pushbutton [package="[SMD]"]
  S3 = Pushbutton [package="[SMD]"]
  8x8_LED_Modul_mit_MAX1 = 8x8 LED Modul mit MAX7219 [package=THT]

nets:
  N1: Mod1.pin_3, Mod1.pin_33, Mod1.pin_38, Mod1.pin_42, S1.Pin_2, S2.Pin_1, S2.Pin_2, S3.Pin_2, 8x8_LED_Modul_mit_MAX1.GND_Eingang
  N2: Mod1.pin_4, 8x8_LED_Modul_mit_MAX1.CLK_Eingang
  N3: Mod1.pin_5, 8x8_LED_Modul_mit_MAX1.DIN_Eingang
  N4: Mod1.pin_7, 8x8_LED_Modul_mit_MAX1.CS_Eingang
  N5: Mod1.pin_14, S1.Pin_3, S1.Pin_4
  N6: Mod1.pin_15, S3.Pin_3, S3.Pin_4
  N7: Mod1.pin_16, S2.Pin_3, S2.Pin_4
  N8: Mod1.pin_40, 8x8_LED_Modul_mit_MAX1.VCC_Eingang

custom parts:
  Raspberry Pi Pico: Raspberry Pi Pico. Based around the RP2040 microcontroller the Pico is a low cost microcontroller device bringing Raspberry Pi quality, cost, and easy of use to the microcontroller space. Jan 2021, Split part in to two versions: tht (this one) and SMD. This one will drill holes for a .1 in header in pcb to allow plugging in the module as well as providing pads to solder the module to the top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
